# Fritzing sketch Untitled Sketch (saved by Fritzing 0.9.3b)
breadboards: 1

parts:
  U1 = NodeMCU V1.0
  Mod1 = KY-019 5V Relay Module [package="Breakout board"]
  hc-sr1 = hc-sr04
  hc-sr2 = hc-sr04
  buz1 = Piezo Buzzer
  12V_LED = LEDs [package=led10mm]
  Switching_Adapter_12V = USB-C plug

nets:
  N1: U1.D2, Mod1.S
  N2: U1.D3, buz1.pin_2
  GND: U1.GND, Mod1.-, hc-sr1.GND, hc-sr2.GND, buz1.pin_1
  N3: U1.D5, hc-sr1.Trig
  N4: U1.D6, hc-sr1.Echo
  N5: U1.D7, hc-sr2.Trig
  N6: U1.D8, hc-sr2.Echo
  VCC: U1.Vin, Mod1.+, hc-sr1.VCC, hc-sr2.VCC
  N7: Mod1.Common, Switching_Adapter_12V.GND
  N8: Mod1.NO, 12V_LED.A
  N9: 12V_LED.C, Switching_Adapter_12V.VCC

custom parts:
  NodeMCU V1.0: ESP8266 based NodeMCU
  KY-019 5V Relay Module: KY-019 5V Relay module, used to control AC circuits.
  Piezo Buzzer: Part from https://www.nutsvolts.com/magazine/article/november2012_SmileysWorkshop modified to be .3 in spacing to match the adafruit buzzer 5V breadboard friendly part.
  USB-C plug: power plug
